# Fritzing sketch fram-tester_breadboard (saved by Fritzing 0.9.3b)
breadboards: 1

parts:
  IC1 = IC, DIP package, 28 pins [chip_label="FRAM (Socket)"]
  U1 = 74HC595 [package="DIP16 [THT]"]
  Teensy_3_1 = Teensy 3.1
  Q1 = PNP-Transistor [package="TO92 [THT]"]
  R1 = Resistor [tolerance=±5% resistance=10k package=THT]

nets:
  A14: IC1.pin1, Teensy_3_1.A0/D14
  A12: IC1.pin2, Teensy_3_1.D12
  A7: IC1.pin3, U1.Q7
  A6: IC1.pin4, U1.Q6
  A5: IC1.pin5, U1.Q5
  A4: IC1.pin6, U1.Q4
  A3: IC1.pin7, U1.Q3
  A2: IC1.pin8, U1.Q2
  A1: IC1.pin9, U1.Q1
  A0: IC1.pin10, U1.Q0
  D0: IC1.pin11, Teensy_3_1.A2/D16
  D1: IC1.pin12, Teensy_3_1.A3/D17
  D2: IC1.pin13, Teensy_3_1.A4/D18
  GND: IC1.pin14, U1.GND, U1.OE, Teensy_3_1.GND
  D3: IC1.pin15, Teensy_3_1.A5/D19
  D4: IC1.pin16, Teensy_3_1.A6/D20
  D5: IC1.pin17, Teensy_3_1.A7/D21
  D6: IC1.pin18, Teensy_3_1.A8/D22
  D7: IC1.pin19, Teensy_3_1.A9/D23
  ^CE: IC1.pin20, Teensy_3_1.D5
  A10: IC1.pin21, Teensy_3_1.D10
  ^OE: IC1.pin22, Teensy_3_1.D4
  A11: IC1.pin23, Teensy_3_1.D11
  A9: IC1.pin24, Teensy_3_1.D9
  A8: IC1.pin25, Teensy_3_1.D8
  A13: IC1.pin26, Teensy_3_1.D13
  ^WE: IC1.pin27, Teensy_3_1.D3
  N1: IC1.pin28, Q1.C
  5V: U1.MR, U1.VCC, Teensy_3_1.Vin, Q1.E, R1.Pin_0
  SH_CP: U1.SH_CP, Teensy_3_1.D2
  ST_CP: U1.ST_CP, Teensy_3_1.D1
  DS: U1.DS, Teensy_3_1.D0
  GOODNIGHT: Teensy_3_1.D6, Q1.B, R1.Pin_1
